# Fritzing sketch Breadboard (saved by Fritzing 0.9.3b)
circuit board: 8.46667cm x 5.64444cm
breadboards: 1

parts:
  WiFi-Witty-Gizwits-ESP-12F1 = WiFi-Witty-Gizwits-ESP-12F
  U1 = RS232 Transceiver [package=dil16]
  Power_plug2 = Power plug
  U3 = Voltage Regulator - 3.3V [package="TO220 [THT]"]
  C1 = Electrolytic Capacitor [capacitance=100nF package="100 mil [THT, electrolytic]"]
  C3 = Electrolytic Capacitor [capacitance=1µF package="100 mil [THT, electrolytic]"]
  C4 = Electrolytic Capacitor [capacitance=1µF package="100 mil [THT, electrolytic]"]
  C5 = Electrolytic Capacitor [capacitance=100nF package="100 mil [THT, electrolytic]"]
  R3 = Resistor [tolerance=±5% resistance=10k package=THT]
  R4 = Resistor [tolerance=±5% resistance=10k package=THT]
  J1 = screw terminal, 3 pins
  Bauteil2 = Logic Level Converter
  C8 = Electrolytic Capacitor [capacitance=0.22mF package="200 mil [THT, electrolytic]"]
  C2 = Electrolytic Capacitor [capacitance=100nF package="100 mil [THT, electrolytic]"]
  C9 = Ceramic Capacitor [capacitance=100nF package="100 mil [THT, multilayer]"]
  C10 = Ceramic Capacitor [capacitance=100nF package="100 mil [THT, multilayer]"]

nets:
  N1: WiFi-Witty-Gizwits-ESP-12F1.REST, R3.Pin_0
  N2: WiFi-Witty-Gizwits-ESP-12F1.CH_PD, R4.Pin_0
  VCC: WiFi-Witty-Gizwits-ESP-12F1.VCC, U1.VCC, U3.output_voltage, C3.+, R3.Pin_1, R4.Pin_1, Bauteil2.LV, C10.0
  GND: WiFi-Witty-Gizwits-ESP-12F1.GND, Power_plug2.GND, U3.GND, C4.+, C5.+, C8.-, C9.1, C10.1
  N3: WiFi-Witty-Gizwits-ESP-12F1.RXD, Bauteil2.RX_HV
  N4: WiFi-Witty-Gizwits-ESP-12F1.TXD, Bauteil2.TX_HV
  N5: U1.C1+, C1.+
  N6: U1.V+, U1.C1-, C1.-, C4.-
  N7: U1.C2+, C2.+
  N8: U1.C2-, C2.-
  N9: U1.V-, C5.-
  N10: U1.T1IN, Bauteil2.TX_LV
  N11: U1.R1OUT, Bauteil2.RX_LV
  N12: U1.R1IN, J1.pin2
  N13: U1.T1OUT, J1.pin1
  N14: U1.GND, C3.-, J1.pin3
  N15: Power_plug2.VCC, U3.input_voltage, Bauteil2.HV, C8.+, C9.0

notes:
  Froeling RX
  Froeling TX
  Froeling GND
  ROT = 5V
  ORANGE = 3.3V

custom parts:
  WiFi-Witty-Gizwits-ESP-12F: A breadboard friendly two part WiFi development board by Gizwits, powered by an ESP8266 ESP-12F SoC, featuring twin micro-usb ports, a photoresistor, a WS2812 RGB-LED and three buttons. The board comes in two parts. The bottom half has reset and flash buttons, a micro-usb with CH340 UART and 2x 1x08 female headers. The top half has the ESP-12F, LDR, RGB-LED, micro-usb (for power only), an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
